// Logisim project EXP 27.circ as structural Verilog: 1 circuit, main circuit main
module main (
  input  in_1,
  input  in_2,
  output out_3,
  output out_4
);

  ExactlyOne xor_1 (.out(out_3), .in0(in_1), .in3(in_2), .in4(in_2));
  and and_1 (out_4, in_1, in_2);
endmodule
